// Logisim project ADD_SUB.circ as structural Verilog: 1 circuit, main circuit ADD_SUB
module ADD_SUB (
  input  B3,
  input  A3,
  input  B2,
  input  A2,
  input  B1,
  input  A1,
  input  B0,
  input  A0,
  input  SUB,
  input  ENABLE,
  output Cout,
  output S0,
  output S3,
  output S2,
  output S1
);

  wire and_1_out, and_2_out, and_3_out, and_4_out, and_5_out, and_6_out, and_7_out, and_8_out, and_9_out,
       and_10_out, and_11_out, and_12_out, C0_out, C1_out, C2_out, xor_1_out, xor_2_out, xor_4_out,
       xor_5_out, xor_6_out, xor_7_out, xor_8_out, xor_9_out;

  xor xor_1 (xor_1_out, B3, SUB);
  ExactlyOne xor_2 (.out(xor_2_out), .in0(xor_1_out), .in1(A3), .in2(C2_out));
  and and_1 (and_1_out, xor_1_out, A3);
  and and_2 (and_2_out, xor_1_out, C2_out);
  and and_3 (and_3_out, A3, C2_out);
  ExactlyOne xor_3 (.out(Cout), .in0(and_3_out), .in1(and_2_out), .in2(and_1_out));
  assign S3 = ENABLE ? xor_2_out : 1'bz;  // Controlled_Buffer controlled_buffer_1
  xor xor_4 (xor_4_out, B2, SUB);
  ExactlyOne xor_5 (.out(xor_5_out), .in0(xor_4_out), .in1(A2), .in2(C1_out));
  and and_4 (and_4_out, xor_4_out, A2);
  and and_5 (and_5_out, A2, C1_out);
  and and_6 (and_6_out, xor_4_out, C1_out);
  ExactlyOne C2 (.out(C2_out), .in0(and_6_out), .in1(and_5_out), .in2(and_4_out));
  assign S2 = ENABLE ? xor_5_out : 1'bz;  // Controlled_Buffer controlled_buffer_2
  xor xor_6 (xor_6_out, B1, SUB);
  and and_7 (and_7_out, xor_6_out, A1);
  and and_8 (and_8_out, xor_6_out, A1);
  and and_9 (and_9_out, A1, C0_out);
  ExactlyOne xor_7 (.out(xor_7_out), .in0(xor_6_out), .in1(A1), .in2(C0_out));
  ExactlyOne C1 (.out(C1_out), .in0(and_9_out), .in1(and_8_out), .in2(and_7_out));
  assign S1 = ENABLE ? xor_7_out : 1'bz;  // Controlled_Buffer controlled_buffer_3
  xor xor_8 (xor_8_out, B0, SUB);
  and and_10 (and_10_out, xor_8_out, A0);
  and and_11 (and_11_out, xor_8_out, SUB);
  and and_12 (and_12_out, A0, SUB);
  ExactlyOne xor_9 (.out(xor_9_out), .in0(xor_8_out), .in1(A0), .in2(SUB));
  ExactlyOne C0 (.out(C0_out), .in0(and_12_out), .in1(and_11_out), .in2(and_10_out));
  assign S0 = ENABLE ? xor_9_out : 1'bz;  // Controlled_Buffer controlled_buffer_4
endmodule
