// Logisim project ASR.circ as structural Verilog: 1 circuit, main circuit main
module main (
  input  a3,
  input  a2,
  input  a1,
  input  a0,
  output shift_off,
  output b0,
  output b1,
  output b2,
  output b3
);


  assign b0 = a1;
  assign b1 = a2;
  assign b2 = a3;
  assign b3 = a3;
  assign shift_off = a0;
endmodule
