// Logisim project FA.circ as structural Verilog: 1 circuit, main circuit FA
module FA (
  input  A,
  input  B,
  input  C_in,
  output Sum,
  output C_out
);

  wire and_1_out, and_2_out, and_3_out;

  and and_1 (and_1_out, A, B);
  and and_2 (and_2_out, A, C_in);
  and and_3 (and_3_out, B, C_in);
  ExactlyOne xor_1 (.out(Sum), .in0(A), .in1(B), .in2(C_in));
  ExactlyOne xor_2 (.out(C_out), .in0(and_1_out), .in1(and_2_out), .in2(and_3_out));
endmodule
