// Logisim project HA.circ as structural Verilog: 1 circuit, main circuit HA
module HA (
  input  A,
  input  B,
  output Sum,
  output Carry
);

  and and_1 (Carry, A, B);
  xor xor_1 (Sum, A, B);
endmodule
