// Logisim project TWOS_COMP.circ as structural Verilog: 1 circuit, main circuit TWOS_COMP
module TWOS_COMP (
  input  a3,
  input  a2,
  input  a1,
  input  a0,
  output b3,
  output b2,
  output b1,
  output b0
);

  wire and_1_out, and_2_out, and_3_out, and_4_out, and_5_out, and_6_out, and_7_out, and_8_out, and_9_out,
       not_1_out, not_2_out, not_3_out, not_4_out;

  not not_1 (not_1_out, a2);
  not not_2 (not_2_out, a3);
  not not_3 (not_3_out, a1);
  not not_4 (not_4_out, a0);
  and and_1 (and_1_out, a3, not_1_out, not_3_out, not_4_out);
  and and_2 (and_2_out, not_2_out, a0);
  and and_3 (and_3_out, not_2_out, a1);
  and and_4 (and_4_out, not_2_out, a2);
  and and_5 (and_5_out, not_1_out, a0);
  and and_6 (and_6_out, not_1_out, a1);
  and and_7 (and_7_out, a2, not_3_out, not_4_out);
  and and_8 (and_8_out, not_3_out, a0);
  and and_9 (and_9_out, a1, not_4_out);
  or or_1 (b3, and_1_out, and_2_out, and_3_out, and_4_out);
  or or_2 (b2, and_5_out, and_6_out, and_7_out);
  or or_3 (b1, and_8_out, and_9_out);

  assign b0 = a0;
endmodule
