// Logisim project XOR4.circ as structural Verilog: 1 circuit, main circuit XOR4
module XOR4 (
  input  a3,
  input  b3,
  input  a1,
  input  b1,
  input  a2,
  input  b2,
  input  a0,
  input  b0,
  output c0,
  output c1,
  output c2,
  output c3
);

  xor xor_1 (c0, b0, a0);
  xor xor_2 (c1, b2, a2);
  xor xor_3 (c2, b1, a1);
  xor xor_4 (c3, b3, a3);
endmodule
