// Logisim project lab_02_03_04_2050.circ as structural Verilog: 8 circuits, main circuit ASL
module ASL (
  input  a3,
  input  a2,
  input  a1,
  input  a0,
  output b0,
  output b1,
  output b2,
  output b3
);

  wire not_1_out;

  not not_1 (not_1_out, a3);
  and and_1 (b0, a3, not_1_out);

  assign b1 = a0;
  assign b2 = a1;
  assign b3 = a2;
endmodule

module ASR (
  input  a3,
  input  a2,
  input  a1,
  input  a0,
  output shift_off,
  output b0,
  output b1,
  output b2,
  output b3
);


  assign b0 = a1;
  assign b1 = a2;
  assign b2 = a3;
  assign b3 = a3;
  assign shift_off = a0;
endmodule

module HA (
  input  A,
  input  B,
  output Sum,
  output Carry
);

  and and_1 (Carry, A, B);
  xor xor_1 (Sum, A, B);
endmodule

module FA (
  input  A,
  input  B,
  input  C_in,
  output Sum,
  output C_out
);

  wire and_1_out, and_2_out, xor_1_out;

  xor xor_1 (xor_1_out, A, B);
  xor xor_2 (Sum, xor_1_out, C_in);
  and and_1 (and_1_out, xor_1_out, C_in);
  and and_2 (and_2_out, A, B);
  or or_1 (C_out, and_1_out, and_2_out);
endmodule

module Compares (
  input  B3,
  input  A3,
  input  B2,
  input  A2,
  input  B1,
  input  A1,
  input  B0,
  input  A0,
  input  SUB,
  input  ENABLE,
  output S2,
  output S1,
  output S0,
  output Cout,
  output S3,
  output LT,
  output GT,
  output EQ
);

  wire fa_1_c_out, fa_1_sum, fa_2_c_out, fa_2_sum, fa_3_c_out, fa_3_sum, fa_4_c_out, fa_4_sum, xor_1_out,
       xor_2_out, xor_3_out, xor_4_out;

  not not_1 (LT, Cout);
  assign Cout = ENABLE ? fa_1_c_out : 1'bz;  // Controlled_Buffer controlled_buffer_1
  xor xor_1 (xor_1_out, B3, SUB);
  FA fa_1 (.A(A3), .B(xor_1_out), .C_in(fa_2_c_out), .Sum(fa_1_sum), .C_out(fa_1_c_out));
  assign S3 = ENABLE ? fa_1_sum : 1'bz;  // Controlled_Buffer controlled_buffer_2
  nor nor_1 (GT, LT, EQ);
  xor xor_2 (xor_2_out, B2, SUB);
  FA fa_2 (.A(A2), .B(xor_2_out), .C_in(fa_3_c_out), .Sum(fa_2_sum), .C_out(fa_2_c_out));
  assign S2 = ENABLE ? fa_2_sum : 1'bz;  // Controlled_Buffer controlled_buffer_3
  nor nor_2 (EQ, S3, S2, S1, S0);
  xor xor_3 (xor_3_out, B1, SUB);
  FA fa_3 (.A(A1), .B(xor_3_out), .C_in(fa_4_c_out), .Sum(fa_3_sum), .C_out(fa_3_c_out));
  assign S1 = ENABLE ? fa_3_sum : 1'bz;  // Controlled_Buffer controlled_buffer_4
  xor xor_4 (xor_4_out, B0, SUB);
  FA fa_4 (.A(A0), .B(xor_4_out), .C_in(SUB), .Sum(fa_4_sum), .C_out(fa_4_c_out));
  assign S0 = ENABLE ? fa_4_sum : 1'bz;  // Controlled_Buffer controlled_buffer_5
endmodule

module XOR4 (
  input  a3,
  input  b3,
  input  a1,
  input  b1,
  input  a2,
  input  b2,
  input  a0,
  input  b0,
  output c0,
  output c1,
  output c2,
  output c3
);

  xor xor_1 (c0, b0, a0);
  xor xor_2 (c1, b2, a2);
  xor xor_3 (c2, b1, a1);
  xor xor_4 (c3, b3, a3);
endmodule

module TWOS_COMP (
  input  a3,
  input  a2,
  input  a1,
  input  a0,
  output b3,
  output b2,
  output b1,
  output b0
);

  wire and_1_out, and_2_out, and_3_out, and_4_out, and_5_out, and_6_out, and_7_out, and_8_out, and_9_out,
       not_1_out, not_2_out, not_3_out, not_4_out;

  not not_1 (not_1_out, a3);
  not not_2 (not_2_out, a2);
  not not_3 (not_3_out, a1);
  not not_4 (not_4_out, a0);
  and and_1 (and_1_out, a3, not_2_out, not_3_out, not_4_out);
  and and_2 (and_2_out, not_1_out, a0);
  and and_3 (and_3_out, not_1_out, a1);
  and and_4 (and_4_out, not_1_out, a2);
  and and_5 (and_5_out, not_2_out, a0);
  and and_6 (and_6_out, not_2_out, a1);
  and and_7 (and_7_out, a2, not_3_out, not_4_out);
  and and_8 (and_8_out, not_3_out, a0);
  and and_9 (and_9_out, a1, not_4_out);
  or or_1 (b3, and_1_out, and_2_out, and_3_out, and_4_out);
  or or_2 (b2, and_5_out, and_6_out, and_7_out);
  or or_3 (b1, and_8_out, and_9_out);

  assign b0 = a0;
endmodule

module ADD_SUB (
  input  B3,
  input  A3,
  input  B2,
  input  A2,
  input  B1,
  input  A1,
  input  B0,
  input  A0,
  input  SUB,
  input  ENABLE,
  output Cout,
  output S3,
  output S2,
  output S1,
  output S0
);

  wire fa_1_c_out, fa_1_sum, fa_2_c_out, fa_2_sum, fa_3_c_out, fa_3_sum, fa_4_c_out, fa_4_sum, xor_1_out,
       xor_2_out, xor_3_out, xor_4_out;

  assign Cout = ENABLE ? fa_1_c_out : 1'bz;  // Controlled_Buffer controlled_buffer_1
  xor xor_1 (xor_1_out, B3, SUB);
  FA fa_1 (.A(A3), .B(xor_1_out), .C_in(fa_2_c_out), .Sum(fa_1_sum), .C_out(fa_1_c_out));
  assign S3 = ENABLE ? fa_1_sum : 1'bz;  // Controlled_Buffer controlled_buffer_2
  xor xor_2 (xor_2_out, B2, SUB);
  FA fa_2 (.A(A2), .B(xor_2_out), .C_in(fa_3_c_out), .Sum(fa_2_sum), .C_out(fa_2_c_out));
  assign S2 = ENABLE ? fa_2_sum : 1'bz;  // Controlled_Buffer controlled_buffer_3
  xor xor_3 (xor_3_out, B1, SUB);
  FA fa_3 (.A(A1), .B(xor_3_out), .C_in(fa_4_c_out), .Sum(fa_3_sum), .C_out(fa_3_c_out));
  assign S1 = ENABLE ? fa_3_sum : 1'bz;  // Controlled_Buffer controlled_buffer_4
  xor xor_4 (xor_4_out, B0, SUB);
  FA fa_4 (.A(A0), .B(xor_4_out), .C_in(SUB), .Sum(fa_4_sum), .C_out(fa_4_c_out));
  assign S0 = ENABLE ? fa_4_sum : 1'bz;  // Controlled_Buffer controlled_buffer_5
endmodule
