// Logisim project lab_05_06_2050.circ as structural Verilog
module SR_GATES (
  input  R,
  input  S,
  output Q,
  output NOT_Q
);

  nor nor_1 (Q, R, NOT_Q);
  nor nor_2 (NOT_Q, Q, S);
endmodule

module SR_LATCH (
  input  S,
  input  R,
  output Q,
  output NOT_Q
);

  _7402 #(.ShowInternalStructure("true")) u_7402_1 (
    .pin1(Q), .pin2(NOT_Q), .pin3(R), .pin4(NOT_Q), .pin5(Q), .pin6(S));  // open: pin13, pin12, pin11, pin10, pin9, pin8
endmodule

module DFF_GATES (
  input  D,
  input  E,
  output out_3,
  output out_4
);

  wire and_1_out, and_2_out, not_1_out;

  not not_1 (not_1_out, D);
  and and_1 (and_1_out, not_1_out, E);
  and and_2 (and_2_out, E, D);
  SR_GATES sr_gates_1 (.R(and_1_out), .S(and_2_out), .Q(out_3), .NOT_Q(out_4));
endmodule

module DFF (
  input  D,
  input  CLK,
  output Q,
  output NOT_Q
);

  wire n7400_1_pin1, n7400_1_pin5, n7400_1_pin10;

  _7400 #(.ShowInternalStructure("true")) u_7400_1 (
    .pin1(n7400_1_pin1), .pin2(NOT_Q), .pin3(Q), .pin4(Q), .pin5(n7400_1_pin5), .pin6(NOT_Q), .pin13(D),
    .pin12(CLK), .pin11(n7400_1_pin1), .pin10(n7400_1_pin10), .pin9(CLK), .pin8(n7400_1_pin5));
  not not_1 (n7400_1_pin10, D);
endmodule

module REG4 (
  input  D0,
  input  D1,
  input  D2,
  input  D3,
  input  ENABLE,
  input  CLK,
  output Q0,
  output Q1,
  output Q2,
  output Q3
);

  wire controlled_buffer_1_out, controlled_buffer_2_out, controlled_buffer_3_out, controlled_buffer_4_out,
       controlled_buffer_5_out, controlled_buffer_6_out, controlled_buffer_7_out, controlled_buffer_8_out;

  assign controlled_buffer_1_out = ENABLE ? D0 : 1'bz;  // Controlled_Buffer controlled_buffer_1
  assign controlled_buffer_2_out = ENABLE ? CLK : 1'bz;  // Controlled_Buffer controlled_buffer_2
  DFF dff_1 (.D(controlled_buffer_1_out), .CLK(controlled_buffer_2_out), .Q(Q0));  // open: NOT_Q
  assign controlled_buffer_3_out = ENABLE ? CLK : 1'bz;  // Controlled_Buffer controlled_buffer_3
  assign controlled_buffer_4_out = ENABLE ? D1 : 1'bz;  // Controlled_Buffer controlled_buffer_4
  DFF dff_2 (.D(controlled_buffer_4_out), .CLK(controlled_buffer_3_out), .Q(Q1));  // open: NOT_Q
  assign controlled_buffer_5_out = ENABLE ? D2 : 1'bz;  // Controlled_Buffer controlled_buffer_5
  assign controlled_buffer_6_out = ENABLE ? CLK : 1'bz;  // Controlled_Buffer controlled_buffer_6
  DFF dff_3 (.D(controlled_buffer_5_out), .CLK(controlled_buffer_6_out), .Q(Q2));  // open: NOT_Q
  assign controlled_buffer_7_out = ENABLE ? D3 : 1'bz;  // Controlled_Buffer controlled_buffer_7
  assign controlled_buffer_8_out = ENABLE ? CLK : 1'bz;  // Controlled_Buffer controlled_buffer_8
  DFF dff_4 (.D(controlled_buffer_7_out), .CLK(controlled_buffer_8_out), .Q(Q3));  // open: NOT_Q
endmodule
