// Logisim project lab_07_2050.circ as structural Verilog
module ALU (
  input  [3:0] I3_I2_I1_I0,
  input  ENABLE,
  input  A3,
  input  A2,
  input  A1,
  input  A0,
  input  B3,
  input  B2,
  input  B1,
  input  B0,
  output LT,
  output GT,
  output EQ,
  output C3,
  output C2,
  output C1,
  output C0
);

  wire decoder_1_out1, decoder_1_out2, decoder_1_out3, decoder_1_out4, decoder_1_out5, decoder_1_out6,
       decoder_1_out7, or_1_out, xor_1_out, xor_2_out;

  Decoder #(.select(4)) decoder_1 (
    .out1(decoder_1_out1), .out2(decoder_1_out2), .out3(decoder_1_out3), .out4(decoder_1_out4),
    .out5(decoder_1_out5), .out6(decoder_1_out6), .out7(decoder_1_out7), .sel(I3_I2_I1_I0), .en(ENABLE));  // open: out0, out8, out9, out10, out11, out12, out13, out14, out15
  or or_1 (or_1_out, decoder_1_out1, decoder_1_out2);
  xor xor_1 (xor_1_out, decoder_1_out2, decoder_1_out3);
  xor xor_2 (xor_2_out, or_1_out, decoder_1_out3);
  XOR4 xor4_1 (
    .ENABLE(decoder_1_out4), .a3(A3), .b3(B3), .a2(A2), .b2(B2), .a1(A1), .b1(B1), .a0(A0), .b0(B0), .c0(C0),
    .c1(C1), .c2(C2), .c3(C3));
  TWOS_COMP twos_comp_1 (
    .a3(A3), .a2(A2), .a1(A1), .a0(A0), .ENABLE(decoder_1_out5), .b3(C3), .b2(C2), .b1(C1), .b0(C0));
  ASL asl_1 (.a3(A3), .a2(A2), .a1(A1), .a0(A0), .ENABLE(decoder_1_out6), .b0(C0), .b1(C1), .b2(C2), .b3(C3));
  ASR asr_1 (
    .ENABLE(decoder_1_out7), .a3(A3), .a2(A2), .a1(A1), .a0(A0), .b0(C0), .b1(C1), .b2(C2), .b3(C3));  // open: shift_off
  Compares compares_1 (
    .B3(B3), .A3(A3), .B2(B2), .A2(A2), .B1(B1), .A1(A1), .B0(B0), .A0(A0), .SUB(xor_1_out),
    .ENABLE(xor_2_out), .ENABLE_COMP(decoder_1_out3), .S2(C2), .S1(C1), .S0(C0), .S3(C3), .LT(LT), .GT(GT),
    .EQ(EQ));  // open: Cout
endmodule

module ASL (
  input  a3,
  input  a2,
  input  a1,
  input  a0,
  input  ENABLE,
  output b0,
  output b1,
  output b2,
  output b3
);

  wire and_1_out, not_1_out;

  not not_1 (not_1_out, a3);
  and and_1 (and_1_out, a3, not_1_out);
  assign b0 = ENABLE ? and_1_out : 1'bz;  // Controlled_Buffer controlled_buffer_1
  assign b1 = ENABLE ? a0 : 1'bz;  // Controlled_Buffer controlled_buffer_2
  assign b2 = ENABLE ? a1 : 1'bz;  // Controlled_Buffer controlled_buffer_3
  assign b3 = ENABLE ? a2 : 1'bz;  // Controlled_Buffer controlled_buffer_4
endmodule

module ASR (
  input  ENABLE,
  input  a3,
  input  a2,
  input  a1,
  input  a0,
  output shift_off,
  output b0,
  output b1,
  output b2,
  output b3
);

  assign shift_off = ENABLE ? a0 : 1'bz;  // Controlled_Buffer controlled_buffer_1
  assign b0 = ENABLE ? a1 : 1'bz;  // Controlled_Buffer controlled_buffer_2
  assign b1 = ENABLE ? a2 : 1'bz;  // Controlled_Buffer controlled_buffer_3
  assign b2 = ENABLE ? a3 : 1'bz;  // Controlled_Buffer controlled_buffer_4
  assign b3 = ENABLE ? a3 : 1'bz;  // Controlled_Buffer controlled_buffer_5
endmodule

module HA (
  input  ENABLE,
  input  A,
  input  B,
  output Sum,
  output Carry
);

  wire and_1_out, xor_1_out;

  and and_1 (and_1_out, A, B);
  xor xor_1 (xor_1_out, A, B);
  assign Sum = ENABLE ? xor_1_out : 1'bz;  // Controlled_Buffer controlled_buffer_1
  assign Carry = ENABLE ? and_1_out : 1'bz;  // Controlled_Buffer controlled_buffer_2
endmodule

module FA (
  input  A,
  input  B,
  input  C_in,
  output Sum,
  output C_out
);

  wire and_1_out, and_2_out, xor_1_out;

  xor xor_1 (xor_1_out, A, B);
  xor xor_2 (Sum, xor_1_out, C_in);
  and and_1 (and_1_out, xor_1_out, C_in);
  and and_2 (and_2_out, A, B);
  or or_1 (C_out, and_1_out, and_2_out);
endmodule

module Compares (
  input  B3,
  input  A3,
  input  B2,
  input  A2,
  input  B1,
  input  A1,
  input  B0,
  input  A0,
  input  SUB,
  input  ENABLE,
  input  ENABLE_COMP,
  output S2,
  output S1,
  output S0,
  output Cout,
  output S3,
  output LT,
  output GT,
  output EQ
);

  wire fa_1_c_out, fa_1_sum, fa_2_c_out, fa_2_sum, fa_3_c_out, fa_3_sum, fa_4_c_out, fa_4_sum, nor_1_out,
       nor_2_out, not_1_out, xor_1_out, xor_2_out, xor_3_out, xor_4_out;

  not not_1 (not_1_out, Cout);
  assign LT = ENABLE_COMP ? not_1_out : 1'bz;  // Controlled_Buffer controlled_buffer_1
  assign Cout = ENABLE ? fa_1_c_out : 1'bz;  // Controlled_Buffer controlled_buffer_2
  xor xor_1 (xor_1_out, B3, SUB);
  FA fa_1 (.A(A3), .B(xor_1_out), .C_in(fa_2_c_out), .Sum(fa_1_sum), .C_out(fa_1_c_out));
  assign S3 = ENABLE ? fa_1_sum : 1'bz;  // Controlled_Buffer controlled_buffer_3
  nor nor_1 (nor_1_out, not_1_out, nor_2_out);
  assign GT = ENABLE_COMP ? nor_1_out : 1'bz;  // Controlled_Buffer controlled_buffer_4
  xor xor_2 (xor_2_out, B2, SUB);
  FA fa_2 (.A(A2), .B(xor_2_out), .C_in(fa_3_c_out), .Sum(fa_2_sum), .C_out(fa_2_c_out));
  assign S2 = ENABLE ? fa_2_sum : 1'bz;  // Controlled_Buffer controlled_buffer_5
  nor nor_2 (nor_2_out, S3, S2, S1, S0);
  assign EQ = ENABLE_COMP ? nor_2_out : 1'bz;  // Controlled_Buffer controlled_buffer_6
  xor xor_3 (xor_3_out, B1, SUB);
  FA fa_3 (.A(A1), .B(xor_3_out), .C_in(fa_4_c_out), .Sum(fa_3_sum), .C_out(fa_3_c_out));
  assign S1 = ENABLE ? fa_3_sum : 1'bz;  // Controlled_Buffer controlled_buffer_7
  xor xor_4 (xor_4_out, B0, SUB);
  FA fa_4 (.A(A0), .B(xor_4_out), .C_in(SUB), .Sum(fa_4_sum), .C_out(fa_4_c_out));
  assign S0 = ENABLE ? fa_4_sum : 1'bz;  // Controlled_Buffer controlled_buffer_8
endmodule

module XOR4 (
  input  ENABLE,
  input  a3,
  input  b3,
  input  a2,
  input  b2,
  input  a1,
  input  b1,
  input  a0,
  input  b0,
  output c0,
  output c1,
  output c2,
  output c3
);

  wire xor_1_out, xor_2_out, xor_3_out, xor_4_out;

  xor xor_1 (xor_1_out, b0, a0);
  xor xor_2 (xor_2_out, b1, a1);
  xor xor_3 (xor_3_out, b2, a2);
  xor xor_4 (xor_4_out, b3, a3);
  assign c0 = ENABLE ? xor_1_out : 1'bz;  // Controlled_Buffer controlled_buffer_1
  assign c1 = ENABLE ? xor_2_out : 1'bz;  // Controlled_Buffer controlled_buffer_2
  assign c2 = ENABLE ? xor_3_out : 1'bz;  // Controlled_Buffer controlled_buffer_3
  assign c3 = ENABLE ? xor_4_out : 1'bz;  // Controlled_Buffer controlled_buffer_4
endmodule

module TWOS_COMP (
  input  a3,
  input  a2,
  input  a1,
  input  a0,
  input  ENABLE,
  output b3,
  output b2,
  output b1,
  output b0
);

  wire and_1_out, and_2_out, and_3_out, and_4_out, and_5_out, and_6_out, and_7_out, and_8_out, and_9_out,
       not_1_out, not_2_out, not_3_out, not_4_out, or_1_out, or_2_out, or_3_out;

  not not_1 (not_1_out, a3);
  not not_2 (not_2_out, a2);
  not not_3 (not_3_out, a1);
  not not_4 (not_4_out, a0);
  and and_1 (and_1_out, a3, not_2_out, not_3_out, not_4_out);
  and and_2 (and_2_out, not_1_out, a0);
  and and_3 (and_3_out, not_1_out, a1);
  and and_4 (and_4_out, not_1_out, a2);
  and and_5 (and_5_out, not_2_out, a0);
  and and_6 (and_6_out, not_2_out, a1);
  and and_7 (and_7_out, a2, not_3_out, not_4_out);
  and and_8 (and_8_out, not_3_out, a0);
  and and_9 (and_9_out, a1, not_4_out);
  or or_1 (or_1_out, and_1_out, and_2_out, and_3_out, and_4_out);
  or or_2 (or_2_out, and_5_out, and_6_out, and_7_out);
  or or_3 (or_3_out, and_8_out, and_9_out);
  assign b3 = ENABLE ? or_1_out : 1'bz;  // Controlled_Buffer controlled_buffer_1
  assign b2 = ENABLE ? or_2_out : 1'bz;  // Controlled_Buffer controlled_buffer_2
  assign b1 = ENABLE ? or_3_out : 1'bz;  // Controlled_Buffer controlled_buffer_3
  assign b0 = ENABLE ? a0 : 1'bz;  // Controlled_Buffer controlled_buffer_4
endmodule

module ADD_SUB (
  input  B3,
  input  A3,
  input  B2,
  input  A2,
  input  B1,
  input  A1,
  input  B0,
  input  A0,
  input  SUB,
  input  ENABLE,
  input  ENABLE_COMP,
  output Cout,
  output S3,
  output S2,
  output S1,
  output S0
);

  wire fa_1_c_out, fa_1_sum, fa_2_c_out, fa_2_sum, fa_3_c_out, fa_3_sum, fa_4_c_out, fa_4_sum, xor_1_out,
       xor_2_out, xor_3_out, xor_4_out;

  assign Cout = ENABLE_COMP ? fa_1_c_out : 1'bz;  // Controlled_Buffer controlled_buffer_1
  xor xor_1 (xor_1_out, B3, SUB);
  FA fa_1 (.A(A3), .B(xor_1_out), .C_in(fa_2_c_out), .Sum(fa_1_sum), .C_out(fa_1_c_out));
  assign S3 = ENABLE_COMP ? fa_1_sum : 1'bz;  // Controlled_Buffer controlled_buffer_2
  xor xor_2 (xor_2_out, B2, SUB);
  FA fa_2 (.A(A2), .B(xor_2_out), .C_in(fa_3_c_out), .Sum(fa_2_sum), .C_out(fa_2_c_out));
  assign S2 = ENABLE_COMP ? fa_2_sum : 1'bz;  // Controlled_Buffer controlled_buffer_3
  xor xor_3 (xor_3_out, B1, SUB);
  FA fa_3 (.A(A1), .B(xor_3_out), .C_in(fa_4_c_out), .Sum(fa_3_sum), .C_out(fa_3_c_out));
  assign S1 = ENABLE_COMP ? fa_3_sum : 1'bz;  // Controlled_Buffer controlled_buffer_4
  xor xor_4 (xor_4_out, B0, SUB);
  FA fa_4 (.A(A0), .B(xor_4_out), .C_in(SUB), .Sum(fa_4_sum), .C_out(fa_4_c_out));
  assign S0 = ENABLE_COMP ? fa_4_sum : 1'bz;  // Controlled_Buffer controlled_buffer_5
endmodule

module test_ALU (
  input  WE,
  input  OE,
  input  WE2,
  input  in_4,
  input  OE2,
  input  in_6,
  input  in_7,
  input  in_8,
  input  in_9,
  input  in_10,
  input  in_11,
  input  [3:0] in_12,
  input  in_13,
  input  CLK,
  output out_15,
  output out_16,
  output out_17,
  output out_18
);

  wire A_q0, A_q1, A_q2, A_q3, alu_1_c0, alu_1_c1, alu_1_c2, alu_1_c3, B_q0, B_q1, B_q2, B_q3, C_q0, C_q1,
       C_q2, C_q3, controlled_buffer_1_out, controlled_buffer_2_out, controlled_buffer_3_out,
       controlled_buffer_4_out, controlled_buffer_5_out, controlled_buffer_6_out, controlled_buffer_7_out,
       controlled_buffer_8_out, controlled_buffer_9_out, controlled_buffer_10_out, controlled_buffer_11_out,
       controlled_buffer_12_out, controlled_buffer_13_out, controlled_buffer_14_out,
       controlled_buffer_15_out, controlled_buffer_16_out, controlled_buffer_17_out,
       controlled_buffer_18_out, controlled_buffer_19_out, controlled_buffer_20_out;

  assign controlled_buffer_1_out = WE ? in_4 : 1'bz;  // Controlled_Buffer controlled_buffer_1
  assign controlled_buffer_2_out = WE ? in_6 : 1'bz;  // Controlled_Buffer controlled_buffer_2
  assign controlled_buffer_3_out = WE ? in_7 : 1'bz;  // Controlled_Buffer controlled_buffer_3
  assign controlled_buffer_4_out = WE ? in_8 : 1'bz;  // Controlled_Buffer controlled_buffer_4
  assign controlled_buffer_5_out = WE ? in_9 : 1'bz;  // Controlled_Buffer controlled_buffer_5
  assign controlled_buffer_6_out = WE ? in_10 : 1'bz;  // Controlled_Buffer controlled_buffer_6
  assign controlled_buffer_7_out = WE ? in_11 : 1'bz;  // Controlled_Buffer controlled_buffer_7
  assign controlled_buffer_8_out = WE ? in_13 : 1'bz;  // Controlled_Buffer controlled_buffer_8
  REG4 A (
    .D0(controlled_buffer_1_out), .D1(controlled_buffer_2_out), .D2(controlled_buffer_3_out),
    .D3(controlled_buffer_4_out), .ENABLE(WE), .CLK(CLK), .Q0(A_q0), .Q1(A_q1), .Q2(A_q2), .Q3(A_q3));
  REG4 B (
    .D0(controlled_buffer_5_out), .D1(controlled_buffer_6_out), .D2(controlled_buffer_7_out),
    .D3(controlled_buffer_8_out), .ENABLE(WE), .CLK(CLK), .Q0(B_q0), .Q1(B_q1), .Q2(B_q2), .Q3(B_q3));
  assign controlled_buffer_9_out = OE ? A_q0 : 1'bz;  // Controlled_Buffer controlled_buffer_9
  assign controlled_buffer_10_out = OE ? A_q1 : 1'bz;  // Controlled_Buffer controlled_buffer_10
  assign controlled_buffer_11_out = OE ? A_q2 : 1'bz;  // Controlled_Buffer controlled_buffer_11
  assign controlled_buffer_12_out = OE ? A_q3 : 1'bz;  // Controlled_Buffer controlled_buffer_12
  assign controlled_buffer_13_out = OE ? B_q0 : 1'bz;  // Controlled_Buffer controlled_buffer_13
  assign controlled_buffer_14_out = OE ? B_q1 : 1'bz;  // Controlled_Buffer controlled_buffer_14
  assign controlled_buffer_15_out = OE ? B_q2 : 1'bz;  // Controlled_Buffer controlled_buffer_15
  assign controlled_buffer_16_out = OE ? B_q3 : 1'bz;  // Controlled_Buffer controlled_buffer_16
  ALU alu_1 (
    .I3_I2_I1_I0(in_12), .ENABLE(OE), .A3(controlled_buffer_12_out), .A2(controlled_buffer_11_out),
    .A1(controlled_buffer_10_out), .A0(controlled_buffer_9_out), .B3(controlled_buffer_16_out),
    .B2(controlled_buffer_15_out), .B1(controlled_buffer_14_out), .B0(controlled_buffer_13_out),
    .C3(alu_1_c3), .C2(alu_1_c2), .C1(alu_1_c1), .C0(alu_1_c0));  // open: LT, GT, EQ
  assign controlled_buffer_17_out = WE2 ? alu_1_c3 : 1'bz;  // Controlled_Buffer controlled_buffer_17
  assign controlled_buffer_18_out = WE2 ? alu_1_c2 : 1'bz;  // Controlled_Buffer controlled_buffer_18
  assign controlled_buffer_19_out = WE2 ? alu_1_c1 : 1'bz;  // Controlled_Buffer controlled_buffer_19
  assign controlled_buffer_20_out = WE2 ? alu_1_c0 : 1'bz;  // Controlled_Buffer controlled_buffer_20
  REG4 C (
    .D0(controlled_buffer_20_out), .D1(controlled_buffer_19_out), .D2(controlled_buffer_18_out),
    .D3(controlled_buffer_17_out), .ENABLE(WE2), .CLK(CLK), .Q0(C_q0), .Q1(C_q1), .Q2(C_q2), .Q3(C_q3));
  assign out_15 = OE2 ? C_q0 : 1'bz;  // Controlled_Buffer controlled_buffer_21
  assign out_16 = OE2 ? C_q1 : 1'bz;  // Controlled_Buffer controlled_buffer_22
  assign out_17 = OE2 ? C_q2 : 1'bz;  // Controlled_Buffer controlled_buffer_23
  assign out_18 = OE2 ? C_q3 : 1'bz;  // Controlled_Buffer controlled_buffer_24
endmodule

module SR_GATES (
  input  R,
  input  S,
  output Q,
  output NOT_Q
);

  nor nor_1 (Q, R, NOT_Q);
  nor nor_2 (NOT_Q, Q, S);
endmodule

module SR_LATCH (
  input  S,
  input  R,
  output Q,
  output NOT_Q
);

  _7402 #(.ShowInternalStructure("true")) u_7402_1 (
    .pin1(Q), .pin2(NOT_Q), .pin3(R), .pin4(NOT_Q), .pin5(Q), .pin6(S));  // open: pin13, pin12, pin11, pin10, pin9, pin8
endmodule

module DFF_GATES (
  input  D,
  input  E,
  output out_3,
  output out_4
);

  wire and_1_out, and_2_out, not_1_out;

  not not_1 (not_1_out, D);
  and and_1 (and_1_out, not_1_out, E);
  and and_2 (and_2_out, E, D);
  SR_GATES sr_gates_1 (.R(and_1_out), .S(and_2_out), .Q(out_3), .NOT_Q(out_4));
endmodule

module DFF (
  input  D,
  input  CLK,
  output Q,
  output NOT_Q
);

  wire n7400_1_pin1, n7400_1_pin5, n7400_1_pin10;

  _7400 #(.ShowInternalStructure("true")) u_7400_1 (
    .pin1(n7400_1_pin1), .pin2(NOT_Q), .pin3(Q), .pin4(Q), .pin5(n7400_1_pin5), .pin6(NOT_Q), .pin13(D),
    .pin12(CLK), .pin11(n7400_1_pin1), .pin10(n7400_1_pin10), .pin9(CLK), .pin8(n7400_1_pin5));
  not not_1 (n7400_1_pin10, D);
endmodule

module REG4 (
  input  D0,
  input  D1,
  input  D2,
  input  D3,
  input  ENABLE,
  input  CLK,
  output Q0,
  output Q1,
  output Q2,
  output Q3
);

  wire controlled_buffer_1_out, controlled_buffer_2_out, controlled_buffer_3_out, controlled_buffer_4_out,
       controlled_buffer_5_out, controlled_buffer_6_out, controlled_buffer_7_out, controlled_buffer_8_out;

  assign controlled_buffer_1_out = ENABLE ? D0 : 1'bz;  // Controlled_Buffer controlled_buffer_1
  assign controlled_buffer_2_out = ENABLE ? CLK : 1'bz;  // Controlled_Buffer controlled_buffer_2
  DFF dff_1 (.D(controlled_buffer_1_out), .CLK(controlled_buffer_2_out), .Q(Q0));  // open: NOT_Q
  assign controlled_buffer_3_out = ENABLE ? CLK : 1'bz;  // Controlled_Buffer controlled_buffer_3
  assign controlled_buffer_4_out = ENABLE ? D1 : 1'bz;  // Controlled_Buffer controlled_buffer_4
  DFF dff_2 (.D(controlled_buffer_4_out), .CLK(controlled_buffer_3_out), .Q(Q1));  // open: NOT_Q
  assign controlled_buffer_5_out = ENABLE ? D2 : 1'bz;  // Controlled_Buffer controlled_buffer_5
  assign controlled_buffer_6_out = ENABLE ? CLK : 1'bz;  // Controlled_Buffer controlled_buffer_6
  DFF dff_3 (.D(controlled_buffer_5_out), .CLK(controlled_buffer_6_out), .Q(Q2));  // open: NOT_Q
  assign controlled_buffer_7_out = ENABLE ? D3 : 1'bz;  // Controlled_Buffer controlled_buffer_7
  assign controlled_buffer_8_out = ENABLE ? CLK : 1'bz;  // Controlled_Buffer controlled_buffer_8
  DFF dff_4 (.D(controlled_buffer_7_out), .CLK(controlled_buffer_8_out), .Q(Q3));  // open: NOT_Q
endmodule
